# Fritzing sketch ControlPIR (saved by Fritzing 0.9.4)
breadboards: 1

parts:
  Keypad4x1 = Keypad Membran 4x4
  Part2 = LCD1602-I2C
  Mod1 = Dragino LoRa Shield V1.4
  Part3 = Arduino Mega 2560 (Rev3)
  S1 = Pushbutton [package="[SMD]"]
  R1 = Resistor [tolerance=±5% resistance=220 package="2512 [SMD]"]
  Part4 = HC-SR501 Body Sensor Module
  Q1 = MOSFET-NCHANNEL [package=to220v]
  R2 = Resistor [tolerance=±5% resistance=220 package="2512 [SMD]"]

nets:
  N1: Keypad4x1.Pin1, Part3.D22
  N2: Keypad4x1.Pin2, Part3.D24
  N3: Keypad4x1.Pin3, Part3.D26
  N4: Keypad4x1.Pin4, Part3.D28
  N5: Keypad4x1.Pin5, Part3.D30
  N6: Keypad4x1.Pin6, Part3.D32
  N7: Keypad4x1.Pin7, Part3.D34
  N8: Keypad4x1.Pin8, Part3.D36
  GND: Part2.GND, Mod1.GND, Part3.GND, R1.Pin_1, Part4.GND, R2.Pin_0
  VCC: Part2.VCC, Mod1.5V, Part3.5V, S1.Pin_3, S1.Pin_4, Part4.VCC, Q1.D
  N9: Part2.SDA, Mod1.SDA, Part3.SDA
  N10: Part2.SCL, Mod1.SCL, Part3.SCL
  N11: Mod1.NC, Part3.IOREF#254
  N12: Mod1.IOREF, Part3.IOREF#255
  N13: Mod1.RST, Part3.RESET
  3V3: Mod1.3V3, Part3.3V3
  VIN: Mod1.VIN, Part3.VIN
  N14: Mod1.A0, Part3.A0, Q1.S, R2.Pin_1
  N15: Mod1.A1, Part3.A1, S1.Pin_1, S1.Pin_2, R1.Pin_0
  N16: Mod1.A2, Part3.A2
  N17: Mod1.A3, Part3.A3
  N18: Mod1.A4, Part3.A4
  N19: Mod1.A5, Part3.A5
  N20: Mod1.DIO0, Mod1.2, Part3.D2_PWM
  N21: Mod1.D12, Mod1.12, Part3.D12_PWM
  N22: Mod1.D11, Mod1.11, Part3.D11_PWM
  N23: Mod1.D13, Mod1.13, Part3.D13_PWM
  N24: Mod1.D8, Mod1.8, Part3.D8_PWM
  N25: Mod1.D7, Mod1.7, Part3.D7_PWM
  N26: Mod1.0, Part3.D0_RX0
  N27: Mod1.1, Part3.D1_TX0
  N28: Mod1.3, Part3.D3_PWM
  N29: Mod1.4, Part3.D4_PWM
  N30: Mod1.5, Part3.D5_PWM
  N31: Mod1.6, Part3.D6_PWM
  N32: Mod1.9, Part3.D9_PWM
  N33: Mod1.10, Part3.D10_PWM
  N34: Mod1.AREF, Part3.AREF
  N35: Part4.OUT, Q1.G

custom parts:
  Keypad Membran 4x4: Membrane Keypad 4x4 Matrix
  LCD1602-I2C: A standard character display, usually with 2x16 characters. Comes in many colors with LCM1602 IIC attached.
  HC-SR501 Body Sensor Module: Pyroelectric Infrared PIR Motion Sensor Detector Module
