# Fritzing sketch NodePIR (saved by Fritzing 0.9.4)
breadboards: 1

parts:
  Part1 = Arduino Uno (Rev3)
  Mod1 = Dragino LoRa Shield V1.4
  Q1 = MOSFET-NCHANNEL [package=to220v]
  Part3 = HC-SR501 Body Sensor Module
  R1 = Resistor [tolerance=±5% resistance=220 package="0603 [SMD]"]

nets:
  N1: Part1.A0, Mod1.A0, Q1.S, R1.Pin_1
  N2: Part1.A1, Mod1.A1
  N3: Part1.A2, Mod1.A2
  N4: Part1.A3, Mod1.A3
  N5: Part1.A4/SDA, Mod1.A4, Mod1.SDA
  N6: Part1.A5/SCL, Mod1.A5, Mod1.SCL
  N7: Part1.D8, Mod1.8
  N8: Part1.D9_PWM, Mod1.9
  N9: Part1.D10_PWM/SS, Mod1.10
  N10: Part1.D11_PWM/MOSI, Mod1.D11, Mod1.11
  N11: Part1.D12/MISO, Mod1.D12, Mod1.12
  N12: Part1.D13/SCK, Mod1.D13, Mod1.13
  GND: Part1.GND, Mod1.GND, Part3.GND, R1.Pin_0
  N13: Part1.AREF, Mod1.AREF
  N14: Part1.D0/RX, Mod1.0
  N15: Part1.D1/TX, Mod1.1
  N16: Part1.D2, Mod1.DIO0, Mod1.2
  N17: Part1.D3_PWM, Mod1.3
  N18: Part1.D4, Mod1.4
  N19: Part1.D5_PWM, Mod1.5
  N20: Part1.D6_PWM, Mod1.6
  N21: Part1.D7, Mod1.7
  N22: Part1.ioref, Mod1.IOREF
  N23: Part1.RESET, Mod1.RST
  3V3: Part1.3V3, Mod1.3V3
  5V: Part1.5V, Mod1.5V, Q1.D, Part3.VCC
  VIN: Part1.VIN, Mod1.VIN
  N24: Part1.N/C, Mod1.NC
  N25: Q1.G, Part3.OUT

custom parts:
  HC-SR501 Body Sensor Module: Pyroelectric Infrared PIR Motion Sensor Detector Module
